# Fritzing sketch schema de cablage (saved by Fritzing 0.9.3b)

parts:
  U1 = Sharp Dust Sensor [part_number=GP2Y1010AU0F]
  M1 = BMP280
  Composant1 = Adafruit I2S Mic - SPH0645 [part_number="Adafruit #3421"]  # not connected
  M2 = TTGO T-Beam V1.1

nets:
  N1: U1.LED, M2.4
  GND: U1.S-GND, M1.GND, M2.GND
  N2: U1.Vo, M2.32
  VCC: U1.VCC, M2.5V
  VIN: M1.VIN, M2.3V3
  N3: M1.SCL, M2.22/SCL
  N4: M1.SDA, M2.21/SDA

custom parts:
  Sharp Dust Sensor: Sharp GP2Y1010AU0F Dust Sensor
  BMP280: Temperature Humidity Barometric presure Sensor, I2C
  Adafruit I2S Mic - SPH0645: For many microcontrollers, adding audio input is easy with one of our analog microphone breakouts. But as you get to bigger and better microcontrollers and microcomputers, you'll find that you don't always have an analog input, or maybe you want to avoid the noise that can seep in with an analog mic system. Once you get past 8-bit micros, you will often find an I2S peripheral, that can take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
  TTGO T-Beam V1.1: LILYGO® TTGO Meshtastic T-Beam V1.1 ESP32 433/868/915/923Mhz WiFi Bluetooth ESP32 GPS NEO-6M SMA 18650 Battery Holder With OLED
